# Fritzing sketch 门禁原理图 (saved by Fritzing 0.9.3b)
breadboards: 1

parts:
  元件1 = RFID-RC522-v2
  元件2 = Arduino Uno (Rev3)
  元件3 = Bluetooth HC-05 Macho
  J1 = Basic Servo

nets:
  N1: 元件1.SDA, 元件2.D10_PWM/SS
  N2: 元件1.SCK, 元件2.D13/SCK
  N3: 元件1.MOSI, 元件2.D11_PWM/MOSI
  N4: 元件1.MISO, 元件2.D12/MISO
  N5: 元件1.GND, 元件2.D9_PWM
  GND: 元件1.RST, 元件2.GND, 元件3.GND, J1.gnd
  3.3V: 元件1.3.3V, 元件2.3V3
  N6: 元件2.D2, 元件3.RXD
  N7: 元件2.D3_PWM, 元件3.TXD
  N8: 元件2.D6_PWM, J1.pulse
  VCC: 元件2.5V, 元件3.VCC, J1.vcc

custom parts:
  RFID-RC522-v2: A simple China made RFID-RC522 Reader; do check the pin labels, as this is a MFRC522 based clone.
