# Fritzing sketch 门禁图示 (saved by Fritzing 0.9.3b)
breadboards: 1

parts:
  元件1 = Arduino Uno (Rev3)
  元件2 = Bluetooth HC-05 Macho
  元件3 = RFID-RC522-v2
  J1 = Basic Servo

nets:
  N1: 元件1.D9_PWM, 元件3.RST
  N2: 元件1.D10_PWM/SS, 元件3.SDA
  N3: 元件1.D11_PWM/MOSI, 元件3.MOSI
  N4: 元件1.D12/MISO, 元件3.MISO
  N5: 元件1.D13/SCK, 元件3.SCK
  GND: 元件1.GND, 元件2.GND, 元件3.GND, J1.gnd
  N6: 元件1.D2, 元件2.TXD
  N7: 元件1.D3_PWM, 元件2.RXD
  N8: 元件1.D6_PWM, J1.pulse
  3V3: 元件1.3V3, 元件3.3.3V
  VCC: 元件1.5V, 元件2.VCC, J1.vcc

custom parts:
  RFID-RC522-v2: A simple China made RFID-RC522 Reader; do check the pin labels, as this is a MFRC522 based clone.
